# Fritzing sketch satcom-relay (saved by Fritzing 0.9.9b)

parts:
  Part3 = Adafruit FeatherWing Proto [part_number="Adafruit #2884"]
  Part5 = Adafruit Feather M0 Basic Proto [part_number="Adafruit #2772"]  # not connected
  Part2 = Adafruit GPS FeatherWing [part_number="Adafruit #3133"]
  J1 = female pin header, 10 pins [form="♀ (female)"]
  Part6 = Lithium Ion Polymer Battery 3.7v 2500mAh [part_number=328]  # not connected
  Part7 = Adafruit FeatherWing Doubler [part_number="Adafruit #2890"]  # not connected
  Part8 = Adafruit FeatherWing Doubler [part_number="Adafruit #2890"]  # not connected
  Part9 = Adafruit Feather M0 Basic Proto [part_number="Adafruit #2772"]  # not connected

nets:
  N1: Part3.G, J1.pin1
  N2: Part3.C, J1.pin4
  N3: Part3.D, Part3.TX, J1.pin5, J1.pin6
  N4: Part3.E, J1.pin7
  N5: Part3.RX, J1.pin9, J1.pin10
  N6: Part3.VBAT, J1.pin2, J1.pin3
  N7: Part2.ENABLE, Part2.A
  N8: Part2.GPS_RX, Part2.MISO
  N9: Part2.GPS_TX, Part2.H

custom parts:
  Adafruit FeatherWing Proto: This is the FeatherWing Proto - a prototyping add-on for all Feather boards. Using our Feather Stacking Headers or Feather Female Headers you can connect a FeatherWing on top or bottom of your Feather board and let the board take flight! This has a duplicate breakout for each pin on a Feather, as well as a bunch of plain grid proto holes. For GND and 3.3V, we give you a strip of connected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
  Adafruit Feather M0 Basic Proto: At the Feather M0's heart is an ATSAMD21G18 ARM Cortex M0 processor, clocked at 48 MHz and at 3.3V logic, the same one used in the new Arduino Zero. This chip has a whopping 256K of FLASH (8x more than the Atmega328 or 32u4) and 32K of RAM (16x as much)! This chip comes with built in USB so it has USB-to-Serial program & debug capability built in with no need for an FTDI-like chip. To make it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
  Adafruit GPS FeatherWing: Give your Feather a sense of place, with an Ultimate GPS FeatherWing. In 2013 we designed the Ultimate GPS module to satisfy all your GPS desires - and now we have brought its power and versatility plus more to our Feather series with the Adafruit Ultimate GPS FeatherWing! This FeatherWing plugs right into your Feather board and gives it a precise, sensitive, and low power GPS module for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
  Lithium Ion Polymer Battery 3.7v 2500mAh: Lithium ion polymer (also known as 'lipo' or 'lipoly') batteries are thin, light and powerful. The output ranges from 4.2V when completely charged to 3.7V. This battery has a capacity of 2500mAh for a total of about 10 Wh. The batteries come pre-attached with a genuine 2-pin JST-PH connector as shown and include the necessary protection circuitry.
  Adafruit FeatherWing Doubler: This is the FeatherWing Doubler - a prototyping add-on and more for all Feather boards. This is similar to our FeatherWing Proto except there are two! The magic of the Doubler comes when stacking a Feather and another board on top of the Doubler so you can work with both boards simultaneously side-by-side! The Doubler, like the Proto, has a duplicate breakout for each pin on a Feather, as well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
